# Fritzing sketch Barcode Authenticator  (Mini) (saved by Fritzing 0.9.3b)

parts:
  Parça1 = Arduino Uno (Rev3)
  S1 = Square Pushbutton
  KY-1 = Keyes Relay [package=THT]
  D2F1 = D2F-FL Omron Snap Action Limit Switch with Level

nets:
  N1: Parça1.D8, KY-1.signal
  N2: Parça1.D2, S1.leg0
  N3: Parça1.5V, S1.leg1, KY-1.power
  N4: Parça1.GND, KY-1.ground
  N5: KY-1.NC, D2F1.NO

notes:
  Normalde Açık Kontak
  Normalde Kapalı Kontak
  24V (+)
  24V (-)
  Sinyal Girişi

custom parts:
  Keyes Relay: The Keyes 5V relay module is suitable for SCM development, home appliance control. It uses a 5V~12V TIL control signal which can control DC / AC signal.
  D2F-FL Omron Snap Action Limit Switch with Level: Snap action switch with stainless steel lever.
